// Logisim project Lazaron-Shyta-DLA.circ as structural Verilog: 1 circuit, main circuit main
module main (
  input  Start_Stop,
  input  Reset,
  input  Screen_On_Off
);

  wire and_1_out, clock_1_out, comparator_1_eq, comparator_2_eq, comparator_3_eq, d_ff_1_q, d_ff_1_qn,
       d_ff_2_q, d_ff_2_qn, d_ff_3_q, d_ff_3_qn;
  wire [3:0] _4, _5, _6, _7, counter_1_q, counter_2_q, counter_3_q, counter_4_q, transistor_1_out,
       transistor_2_out, transistor_3_out, transistor_4_out;

  Clock clock_1 (.out(clock_1_out));
  D_Flip_Flop d_ff_1 (.clk(clock_1_out), .D(d_ff_1_qn), .Q(d_ff_1_q), .Qn(d_ff_1_qn));  // open: preset, en, reset
  D_Flip_Flop d_ff_2 (.clk(d_ff_1_q), .D(d_ff_2_qn), .Q(d_ff_2_q), .Qn(d_ff_2_qn));  // open: preset, en, reset
  D_Flip_Flop d_ff_3 (.clk(d_ff_2_q), .D(d_ff_3_qn), .Q(d_ff_3_q), .Qn(d_ff_3_qn));  // open: preset, en, reset
  buf and_1 (and_1_out, Start_Stop);  // AND_Gate
  Hex_Digit_Display hex_digit_display_1 (.value(transistor_1_out));  // open: dp
  Transistor #(.width(4)) transistor_1 (.in(_7), .out(transistor_1_out), .gate(Screen_On_Off));
  Transistor #(.width(4)) transistor_2 (.in(_6), .out(transistor_2_out), .gate(Screen_On_Off));
  Counter #(.width(4), .max('h9)) counter_1 (
    .count(and_1_out), .Q(counter_1_q), .clk(d_ff_3_q), .clr(Reset));  // open: load, D, carry
  Hex_Digit_Display hex_digit_display_2 (.value(transistor_2_out), .dp(1'b1));
  Transistor #(.width(4)) transistor_3 (.in(_5), .out(transistor_3_out), .gate(Screen_On_Off));
  Counter #(.width(4), .max('h9)) counter_2 (
    .count(and_1_out), .Q(counter_2_q), .clk(comparator_1_eq), .clr(Reset));  // open: load, D, carry
  Counter #(.width(4), .max('h9)) counter_3 (
    .count(and_1_out), .Q(counter_3_q), .clk(comparator_2_eq), .clr(Reset));  // open: load, D, carry
  Counter #(.width(4), .max('h9)) counter_4 (
    .count(and_1_out), .Q(counter_4_q), .clk(comparator_3_eq), .clr(Reset));  // open: load, D, carry
  Hex_Digit_Display hex_digit_display_3 (.value(transistor_4_out));  // open: dp
  Hex_Digit_Display hex_digit_display_4 (.value(transistor_3_out));  // open: dp
  Transistor #(.width(4)) transistor_4 (.in(_4), .out(transistor_4_out), .gate(Screen_On_Off));
  Comparator #(.width(4)) comparator_1 (.a(counter_1_q), .b(4'b0000), .eq(comparator_1_eq));  // open: gt, lt
  Comparator #(.width(4)) comparator_2 (.a(counter_2_q), .b(4'b0000), .eq(comparator_2_eq));  // open: gt, lt
  Comparator #(.width(4)) comparator_3 (.a(counter_3_q), .b(4'b0000), .eq(comparator_3_eq));  // open: gt, lt
  Multiplexer #(.width(4)) multiplexer_1 (.in0(counter_1_q), .in1(counter_1_q), .out(_4), .sel(and_1_out));  // open: en
  Multiplexer #(.width(4)) multiplexer_2 (.in0(counter_2_q), .in1(counter_2_q), .out(_5), .sel(and_1_out));  // open: en
  Multiplexer #(.width(4)) multiplexer_3 (.in0(counter_3_q), .in1(counter_3_q), .out(_6), .sel(and_1_out));  // open: en
  Multiplexer #(.width(4)) multiplexer_4 (.in0(counter_4_q), .in1(counter_4_q), .out(_7), .sel(and_1_out));  // open: en

  // Other names for the same wires on the sheet: _1 = Start_Stop; _2 = Reset; _3 = Screen_On_Off

  // Notes on the sheet:
  //   Fall 2018
  //                Lazaron Shyta / Enio Bitri  
  //   StopWatch DLA Assignment
  //   Computer Architecture
  //   100195078 / 100169572
endmodule
